# Fritzing sketch GarDoor-Carv2.00 (saved by Fritzing 0.9.3b)
breadboards: 1

parts:
  U1 = NodeMCU V1.0
  Part1 = DHT22 module  # not connected
  KY-1 = Keyes Relay [package=THT]
  Part2 = SRF05 Ultrasonic Rangefinder
  Part3 = SRF05 Ultrasonic Rangefinder

nets:
  N1: U1.D1, Part2.Echo
  N2: U1.D2, Part3.Echo
  VCC: U1.3V3, Part2.VCC, Part3.VCC
  GND: U1.GND, KY-1.ground, Part2.GND, Part3.GND
  N3: U1.D5, Part2.Trig, Part3.Trig
  N4: U1.D6, KY-1.signal
  N5: U1.Vin, KY-1.power

custom parts:
  NodeMCU V1.0: ESP8266 based NodeMCU
  Keyes Relay: The Keyes 5V relay module is suitable for SCM development, home appliance control. It uses a 5V~12V TIL control signal which can control DC / AC signal.
